// Logisim project MIPSpipeline.circ as structural Verilog: 14 circuits, main circuit main
module main (
  output [4:0] out_1,
  output [4:0] out_2,
  output [1:0] out_3,
  output [31:0] out_4,
  output [4:0] out_5,
  output [31:0] out_6,
  output [31:0] out_7,
  output [1:0] out_8,
  output [4:0] out_9,
  output [4:0] out_10,
  output [31:0] out_11,
  output [4:0] out_12,
  output [31:0] out_13,
  output [31:0] out_14,
  output [31:0] out_15
);

  wire adder_1_cout, adder_2_cout, alu_1_zero, and_1_out, and_2_out, CLK, ex_mem_1_out_13, ex_mem_1_out_14,
       ex_mem_1_out_15, ex_mem_1_out_16, ex_mem_1_out_17, ex_mem_1_out_18, ex_mem_1_out_19,
       hazardunit_1_flush, hazardunit_1_if_idwrite, hazardunit_1_pcwrite, id_ex_1_out_19, id_ex_1_out_20,
       id_ex_1_out_21, id_ex_1_out_22, id_ex_1_out_23, id_ex_1_out_24, id_ex_1_out_25, id_ex_1_out_28,
       jumpcontrol_1_jump, mem_wb_1_out_7, mem_wb_1_out_8, multiplexer_7_out;
  wire [3:0] controlunit_1_out_10, id_ex_1_out_26;
  wire [4:0] ex_mem_1_out_23, id_ex_1_out_27, id_ex_1_out_35, intructionformater_1_out_3, mem_wb_1_out_11;
  wire [5:0] intructionformater_1_out_2, intructionformater_1_out_8;
  wire [15:0] adder_1_out, adder_2_out, ex_mem_1_out_21, id_ex_1_out_31, id_ex_1_out_32, if_id_1_out_6,
       intructionformater_1_out_5, jumpcontrol_1_out_2, multiplexer_1_out, multiplexer_2_out, register_1_q,
       shifter_1_out;
  wire [16:0] controlunit_1_memread, multiplexer_3_out;
  wire [31:0] dm_1_out_6, ex_mem_1_out_20, ex_mem_1_out_22, id_ex_1_out_29, id_ex_1_out_30, if_id_1_out_5,
       mem_wb_1_out_9, mem_wb_1_out_10, multiplexer_6_out, multiplexer_9_out;

  Multiplexer #(.width(16)) multiplexer_1 (
    .in0(adder_1_out), .in1(ex_mem_1_out_21), .out(multiplexer_1_out), .sel(multiplexer_7_out));
  Multiplexer #(.width(16)) multiplexer_2 (
    .in0(multiplexer_1_out), .in1(jumpcontrol_1_out_2), .out(multiplexer_2_out), .sel(jumpcontrol_1_jump));
  Clock clock_1 (.out(CLK));
  Register #(.width(16)) register_1 (
    .D(multiplexer_2_out), .en(hazardunit_1_pcwrite), .clk(CLK), .Q(register_1_q));  // open: clr
  JumpControl jumpcontrol_1 (.in_1(out_4), .out_2(jumpcontrol_1_out_2), .Jump(jumpcontrol_1_jump));
  Adder #(.width(16)) adder_1 (.a(register_1_q), .b(16'h4), .out(adder_1_out), .cin(1'b0), .cout(adder_1_cout));
  IM im_1 (.in_1(register_1_q), .out_2(out_4));
  IF_ID if_id_1 (
    .in_2(out_4), .in_3(adder_1_out), .in_1(hazardunit_1_if_idwrite), .in_4(CLK), .out_5(if_id_1_out_5),
    .out_6(if_id_1_out_6));
  IntructionFormater intructionformater_1 (
    .in_1(if_id_1_out_5), .out_6(out_9), .out_7(out_5), .out_8(intructionformater_1_out_8),
    .out_2(intructionformater_1_out_2), .out_3(intructionformater_1_out_3), .out_4(out_12),
    .out_5(intructionformater_1_out_5));
  ControlUnit controlunit_1 (
    .OPcode(intructionformater_1_out_8), .Funct(intructionformater_1_out_2),
    .MemRead(controlunit_1_memread[0]), .MemWrite(controlunit_1_memread[1]),
    .MemToReg(controlunit_1_memread[2]), .RegWrite(controlunit_1_memread[3]),
    .RegDst(controlunit_1_memread[4]), .Branch(controlunit_1_memread[5]), .ALUsrc(controlunit_1_memread[6]),
    .out_10(controlunit_1_out_10), .BNE(controlunit_1_memread[16]));
  Multiplexer #(.width(17)) multiplexer_3 (
    .in0({controlunit_1_memread[16], intructionformater_1_out_3, controlunit_1_out_10, controlunit_1_memread[6:0]}),
    .in1({17{1'b0}}), .out(multiplexer_3_out), .sel(hazardunit_1_flush));
  registers registers_1 (
    .in_1(out_5), .in_4(out_9), .in_5(mem_wb_1_out_8), .in_6(mem_wb_1_out_11), .CLK(CLK),
    .in_3(multiplexer_9_out), .out_7(out_7), .out_8(out_11));
  HazardUnit hazardunit_1 (
    .in_1(out_10), .in_3(if_id_1_out_5), .MemRead(id_ex_1_out_19), .IF_IDwrite(hazardunit_1_if_idwrite),
    .Flush(hazardunit_1_flush), .PCwrite(hazardunit_1_pcwrite));
  ID_EX id_ex_1 (
    .in_1(multiplexer_3_out[0]), .in_2(multiplexer_3_out[1]), .in_3(multiplexer_3_out[2]),
    .RegWrite(multiplexer_3_out[3]), .RegDst(multiplexer_3_out[4]), .Branch(multiplexer_3_out[5]),
    .ALUsrc(multiplexer_3_out[6]), .in_8(multiplexer_3_out[10:7]), .in_9(multiplexer_3_out[15:11]),
    .BNE(multiplexer_3_out[16]), .in_15(out_5), .in_16(out_9), .in_17(out_12), .in_11(out_7), .in_12(out_11),
    .in_13(intructionformater_1_out_5), .in_14(if_id_1_out_6), .CLK(CLK), .out_33(out_1), .out_34(out_2),
    .out_35(id_ex_1_out_35), .out_29(id_ex_1_out_29), .out_30(id_ex_1_out_30), .out_31(id_ex_1_out_31),
    .out_32(id_ex_1_out_32), .out_19(id_ex_1_out_19), .out_20(id_ex_1_out_20), .out_21(id_ex_1_out_21),
    .out_22(id_ex_1_out_22), .out_23(id_ex_1_out_23), .out_24(id_ex_1_out_24), .out_25(id_ex_1_out_25),
    .out_26(id_ex_1_out_26), .out_27(id_ex_1_out_27), .out_28(id_ex_1_out_28));
  Multiplexer #(.width(5)) multiplexer_4 (.in0(id_ex_1_out_35), .in1(out_2), .out(out_10), .sel(id_ex_1_out_23));
  assign out_13 = {{16{id_ex_1_out_31[15]}}, id_ex_1_out_31};  // Bit_Extender bit_extender_1
  Shifter #(.width(16)) shifter_1 (.in(id_ex_1_out_31), .\dist (4'b0010), .out(shifter_1_out));
  Adder #(.width(16)) adder_2 (
    .a(id_ex_1_out_32), .b(shifter_1_out), .out(adder_2_out), .cin(1'b0), .cout(adder_2_cout));
  Multiplexer #(.select(2), .width(32)) multiplexer_5 (
    .in0(id_ex_1_out_29), .in1(ex_mem_1_out_20), .in2(multiplexer_9_out), .in3(multiplexer_9_out),
    .out(out_14), .sel(out_3));
  Multiplexer #(.select(2), .width(32)) multiplexer_6 (
    .in0(id_ex_1_out_30), .in1(ex_mem_1_out_20), .in2(multiplexer_9_out), .in3(multiplexer_9_out),
    .out(multiplexer_6_out), .sel(out_8));
  ForwardingUnit forwardingunit_1 (
    .in_2(out_1), .in_3(ex_mem_1_out_23), .in_4(mem_wb_1_out_11), .in_5(out_2), .WBRW(mem_wb_1_out_8),
    .MemRW(ex_mem_1_out_16), .out_7(out_3), .ForwrdB(out_8));
  Multiplexer multiplexer_7 (.in0(and_2_out), .in1(and_1_out), .out(multiplexer_7_out), .sel(ex_mem_1_out_18));
  Multiplexer #(.width(32)) multiplexer_8 (.in0(multiplexer_6_out), .in1(out_13), .out(out_15), .sel(id_ex_1_out_25));
  ALU alu_1 (
    .in_3(id_ex_1_out_27), .in_1(out_14), .in_2(out_15), .in_4(id_ex_1_out_26), .ZERO(alu_1_zero),
    .out_6(out_6));  // open: out_7
  and and_1 (and_1_out, ex_mem_1_out_18, ~ex_mem_1_out_19);  // AND_Gate
  and and_2 (and_2_out, ex_mem_1_out_19, ex_mem_1_out_17);
  EX_MEM ex_mem_1 (
    .in_10(multiplexer_6_out), .in_11(out_10), .CLK(CLK), .in_9(adder_2_out), .in_1(id_ex_1_out_19),
    .in_2(id_ex_1_out_20), .in_3(id_ex_1_out_21), .in_4(id_ex_1_out_22), .Branch(id_ex_1_out_24),
    .BNE(id_ex_1_out_28), .Zero(alu_1_zero), .in_8(out_6), .out_22(ex_mem_1_out_22),
    .out_23(ex_mem_1_out_23), .out_13(ex_mem_1_out_13), .out_14(ex_mem_1_out_14), .out_15(ex_mem_1_out_15),
    .out_16(ex_mem_1_out_16), .out_17(ex_mem_1_out_17), .out_18(ex_mem_1_out_18), .out_19(ex_mem_1_out_19),
    .out_20(ex_mem_1_out_20), .out_21(ex_mem_1_out_21));
  DM dm_1 (
    .CLK(CLK), .in_3(ex_mem_1_out_13), .in_1(ex_mem_1_out_20), .in_5(ex_mem_1_out_22),
    .in_2(ex_mem_1_out_14), .out_6(dm_1_out_6));
  MEM_WB mem_wb_1 (
    .in_5(ex_mem_1_out_23), .in_1(ex_mem_1_out_15), .in_2(ex_mem_1_out_16), .in_3(dm_1_out_6),
    .in_4(ex_mem_1_out_20), .CLK(CLK), .out_7(mem_wb_1_out_7), .out_8(mem_wb_1_out_8),
    .out_9(mem_wb_1_out_9), .out_10(mem_wb_1_out_10), .out_11(mem_wb_1_out_11));
  Multiplexer #(.width(32)) multiplexer_9 (
    .in0(mem_wb_1_out_10), .in1(mem_wb_1_out_9), .out(multiplexer_9_out), .sel(mem_wb_1_out_7));
  // also tied to GND on the sheet: {adder_1_cout, adder_2_cout}

  // Notes on the sheet:
  //   PC
endmodule

module registers (
  input  [4:0] in_1,
  input  CLK,
  input  [31:0] in_3,
  input  [4:0] in_4,
  input  in_5,
  input  [4:0] in_6,
  output [31:0] out_7,
  output [31:0] out_8
);

  wire demultiplexer_1_out1, demultiplexer_1_out2, demultiplexer_1_out3, demultiplexer_1_out4,
       demultiplexer_1_out5, demultiplexer_1_out6, demultiplexer_1_out7, demultiplexer_1_out8,
       demultiplexer_1_out9, demultiplexer_1_out10, demultiplexer_1_out11, demultiplexer_1_out12,
       demultiplexer_1_out13, demultiplexer_1_out14, demultiplexer_1_out15, demultiplexer_1_out16,
       demultiplexer_1_out17, demultiplexer_1_out18, demultiplexer_1_out19, demultiplexer_1_out20,
       demultiplexer_1_out21, demultiplexer_1_out22, demultiplexer_1_out23, demultiplexer_1_out24,
       demultiplexer_1_out25, demultiplexer_1_out26, demultiplexer_1_out27, demultiplexer_1_out28,
       demultiplexer_1_out29, demultiplexer_1_out30, demultiplexer_1_out31, not_1_out;
  wire [31:0] register_1_q, register_2_q, register_3_q, register_4_q, register_5_q, register_6_q,
       register_7_q, register_8_q, register_9_q, register_10_q, register_11_q, register_12_q, register_13_q,
       register_14_q, register_15_q, register_16_q, register_17_q, register_18_q, register_19_q,
       register_20_q, register_21_q, register_22_q, register_23_q, register_24_q, register_25_q,
       register_26_q, register_27_q, register_28_q, register_29_q, register_30_q, register_31_q,
       register_32_q;

  Demultiplexer #(.select(5)) demultiplexer_1 (
    .out1(demultiplexer_1_out1), .out2(demultiplexer_1_out2), .out3(demultiplexer_1_out3),
    .out4(demultiplexer_1_out4), .out5(demultiplexer_1_out5), .out6(demultiplexer_1_out6),
    .out7(demultiplexer_1_out7), .out8(demultiplexer_1_out8), .out9(demultiplexer_1_out9),
    .out10(demultiplexer_1_out10), .out11(demultiplexer_1_out11), .out12(demultiplexer_1_out12),
    .out13(demultiplexer_1_out13), .out14(demultiplexer_1_out14), .out15(demultiplexer_1_out15),
    .out16(demultiplexer_1_out16), .out17(demultiplexer_1_out17), .out18(demultiplexer_1_out18),
    .out19(demultiplexer_1_out19), .out20(demultiplexer_1_out20), .out21(demultiplexer_1_out21),
    .out22(demultiplexer_1_out22), .out23(demultiplexer_1_out23), .out24(demultiplexer_1_out24),
    .out25(demultiplexer_1_out25), .out26(demultiplexer_1_out26), .out27(demultiplexer_1_out27),
    .out28(demultiplexer_1_out28), .out29(demultiplexer_1_out29), .out30(demultiplexer_1_out30),
    .out31(demultiplexer_1_out31), .in(in_5), .sel(in_6));  // open: out0
  not not_1 (not_1_out, CLK);
  Register #(.width(32)) register_1 (.D(in_3), .en(1'b0), .clk(not_1_out), .Q(register_1_q));  // open: clr
  Register #(.width(32)) register_2 (
    .D(in_3), .en(demultiplexer_1_out1), .clk(not_1_out), .Q(register_2_q));  // open: clr
  Register #(.width(32)) register_3 (
    .D(in_3), .en(demultiplexer_1_out2), .clk(not_1_out), .Q(register_3_q));  // open: clr
  Register #(.width(32)) register_4 (
    .D(in_3), .en(demultiplexer_1_out3), .clk(not_1_out), .Q(register_4_q));  // open: clr
  Register #(.width(32)) register_5 (
    .D(in_3), .en(demultiplexer_1_out4), .clk(not_1_out), .Q(register_5_q));  // open: clr
  Register #(.width(32)) register_6 (
    .D(in_3), .en(demultiplexer_1_out5), .clk(not_1_out), .Q(register_6_q));  // open: clr
  Register #(.width(32)) register_7 (
    .D(in_3), .en(demultiplexer_1_out6), .clk(not_1_out), .Q(register_7_q));  // open: clr
  Register #(.width(32)) register_8 (
    .D(in_3), .en(demultiplexer_1_out7), .clk(not_1_out), .Q(register_8_q));  // open: clr
  Register #(.width(32)) register_9 (
    .D(in_3), .en(demultiplexer_1_out8), .clk(not_1_out), .Q(register_9_q));  // open: clr
  Register #(.width(32)) register_10 (
    .D(in_3), .en(demultiplexer_1_out9), .clk(not_1_out), .Q(register_10_q));  // open: clr
  Register #(.width(32)) register_11 (
    .D(in_3), .en(demultiplexer_1_out10), .clk(not_1_out), .Q(register_11_q));  // open: clr
  Register #(.width(32)) register_12 (
    .D(in_3), .en(demultiplexer_1_out11), .clk(not_1_out), .Q(register_12_q));  // open: clr
  Register #(.width(32)) register_13 (
    .D(in_3), .en(demultiplexer_1_out12), .clk(not_1_out), .Q(register_13_q));  // open: clr
  Register #(.width(32)) register_14 (
    .D(in_3), .en(demultiplexer_1_out13), .clk(not_1_out), .Q(register_14_q));  // open: clr
  Register #(.width(32)) register_15 (
    .D(in_3), .en(demultiplexer_1_out14), .clk(not_1_out), .Q(register_15_q));  // open: clr
  Register #(.width(32)) register_16 (
    .D(in_3), .en(demultiplexer_1_out15), .clk(not_1_out), .Q(register_16_q));  // open: clr
  Register #(.width(32)) register_17 (
    .D(in_3), .en(demultiplexer_1_out16), .clk(not_1_out), .Q(register_17_q));  // open: clr
  Register #(.width(32)) register_18 (
    .D(in_3), .en(demultiplexer_1_out17), .clk(not_1_out), .Q(register_18_q));  // open: clr
  Register #(.width(32)) register_19 (
    .D(in_3), .en(demultiplexer_1_out18), .clk(not_1_out), .Q(register_19_q));  // open: clr
  Register #(.width(32)) register_20 (
    .D(in_3), .en(demultiplexer_1_out19), .clk(not_1_out), .Q(register_20_q));  // open: clr
  Register #(.width(32)) register_21 (
    .D(in_3), .en(demultiplexer_1_out20), .clk(not_1_out), .Q(register_21_q));  // open: clr
  Register #(.width(32)) register_22 (
    .D(in_3), .en(demultiplexer_1_out21), .clk(not_1_out), .Q(register_22_q));  // open: clr
  Register #(.width(32)) register_23 (
    .D(in_3), .en(demultiplexer_1_out22), .clk(not_1_out), .Q(register_23_q));  // open: clr
  Register #(.width(32)) register_24 (
    .D(in_3), .en(demultiplexer_1_out23), .clk(not_1_out), .Q(register_24_q));  // open: clr
  Register #(.width(32)) register_25 (
    .D(in_3), .en(demultiplexer_1_out24), .clk(not_1_out), .Q(register_25_q));  // open: clr
  Register #(.width(32)) register_26 (
    .D(in_3), .en(demultiplexer_1_out25), .clk(not_1_out), .Q(register_26_q));  // open: clr
  Register #(.width(32)) register_27 (
    .D(in_3), .en(demultiplexer_1_out26), .clk(not_1_out), .Q(register_27_q));  // open: clr
  Register #(.width(32)) register_28 (
    .D(in_3), .en(demultiplexer_1_out27), .clk(not_1_out), .Q(register_28_q));  // open: clr
  Register #(.width(32)) register_29 (
    .D(in_3), .en(demultiplexer_1_out28), .clk(not_1_out), .Q(register_29_q));  // open: clr
  Register #(.width(32)) register_30 (
    .D(in_3), .en(demultiplexer_1_out29), .clk(not_1_out), .Q(register_30_q));  // open: clr
  Register #(.width(32)) register_31 (
    .D(in_3), .en(demultiplexer_1_out30), .clk(not_1_out), .Q(register_31_q));  // open: clr
  Register #(.width(32)) register_32 (
    .D(in_3), .en(demultiplexer_1_out31), .clk(not_1_out), .Q(register_32_q));  // open: clr
  Multiplexer #(.select(5), .width(32)) multiplexer_1 (
    .in0(register_1_q), .in1(register_2_q), .in2(register_3_q), .in3(register_4_q), .in4(register_5_q),
    .in5(register_6_q), .in6(register_7_q), .in7(register_8_q), .in8(register_9_q), .in9(register_10_q),
    .in10(register_11_q), .in11(register_12_q), .in12(register_13_q), .in13(register_14_q),
    .in14(register_15_q), .in15(register_16_q), .in16(register_17_q), .in17(register_18_q),
    .in18(register_19_q), .in19(register_20_q), .in20(register_21_q), .in21(register_22_q),
    .in22(register_23_q), .in23(register_24_q), .in24(register_25_q), .in25(register_26_q),
    .in26(register_27_q), .in27(register_28_q), .in28(register_29_q), .in29(register_30_q),
    .in30(register_31_q), .in31(register_32_q), .out(out_7), .sel(in_1));
  Multiplexer #(.select(5), .width(32)) multiplexer_2 (
    .in0(register_1_q), .in1(register_2_q), .in2(register_3_q), .in3(register_4_q), .in4(register_5_q),
    .in5(register_6_q), .in6(register_7_q), .in7(register_8_q), .in8(register_9_q), .in9(register_10_q),
    .in10(register_11_q), .in11(register_12_q), .in12(register_13_q), .in13(register_14_q),
    .in14(register_15_q), .in15(register_16_q), .in16(register_17_q), .in17(register_18_q),
    .in18(register_19_q), .in19(register_20_q), .in20(register_21_q), .in21(register_22_q),
    .in22(register_23_q), .in23(register_24_q), .in24(register_25_q), .in25(register_26_q),
    .in26(register_27_q), .in27(register_28_q), .in28(register_29_q), .in29(register_30_q),
    .in30(register_31_q), .in31(register_32_q), .out(out_8), .sel(in_4));

  // Notes on the sheet:
  //   RegWrite
  //   RD
  //   Data
  //   RS
  //   RT
  //   A
  //   B
endmodule

module ALU (
  input  [31:0] in_1,
  input  [31:0] in_2,
  input  [4:0] in_3,
  input  [3:0] in_4,
  output ZERO,
  output [31:0] out_6,
  output [31:0] out_7
);

  wire comparator_1_lt;
  wire [31:0] adder_1_out, and_1_out, not_1_out, or_1_out, or_2_out, shifter_1_out, shifter_2_out,
       shifter_3_out, subtractor_1_out, xor_1_out;

  Adder #(.width(32)) adder_1 (.a(in_1), .b(in_2), .out(adder_1_out));  // open: cin, cout
  Subtractor #(.width(32)) subtractor_1 (.a(in_1), .b(in_2), .out(subtractor_1_out));  // open: bin, bout
  Shifter #(.width(32)) shifter_1 (.in(in_2), .\dist (in_3), .out(shifter_1_out));
  Shifter #(.shift("lr"), .width(32)) shifter_2 (.in(in_2), .\dist (in_3), .out(shifter_2_out));
  Shifter #(.shift("ar"), .width(32)) shifter_3 (.in(in_2), .\dist (in_3), .out(shifter_3_out));
  assign and_1_out = in_1 & in_2;  // AND_Gate and_1, 32 bits wide
  assign or_1_out = in_1 | in_2;  // OR_Gate or_1, 32 bits wide
  assign xor_1_out = in_1 ^ in_2;  // XOR_Gate xor_1, 32 bits wide
  assign or_2_out = in_1 | in_2;  // OR_Gate or_2, 32 bits wide
  Comparator #(.width(32)) comparator_1 (.a(in_1), .b(in_2), .lt(comparator_1_lt));  // open: gt, eq
  assign not_1_out = ~or_2_out;  // NOT_Gate not_1, 32 bits wide
  assign out_7 = {{31{1'b0}}, comparator_1_lt};  // Bit_Extender bit_extender_1
  Multiplexer #(.select(4), .width(32)) multiplexer_1 (
    .in0(adder_1_out), .in1(and_1_out), .in2(not_1_out), .in3(or_1_out), .in4(out_7), .in5(shifter_1_out),
    .in6(shifter_2_out), .in7(shifter_3_out), .in8(subtractor_1_out), .in9(xor_1_out), .in10({32{1'b0}}),
    .in11({32{1'b0}}), .in12({32{1'b0}}), .in13({32{1'b0}}), .in14({32{1'b0}}), .in15({32{1'b0}}),
    .out(out_6), .sel(in_4));
  nor nor_1 (ZERO, out_6[0], out_6[1], out_6[2], out_6[3], out_6[4], out_6[5], out_6[6], out_6[7], out_6[8], out_6[9], out_6[10], out_6[11], out_6[12], out_6[13], out_6[14], out_6[15], out_6[16], out_6[17], out_6[18], out_6[19], out_6[20], out_6[21], out_6[22], out_6[23], out_6[24], out_6[25], out_6[26], out_6[27], out_6[28], out_6[29], out_6[30], out_6[31]);

  // Notes on the sheet:
  //   A
  //   B
  //   SHAMT
  //   ALUOP
  //   S
endmodule

module IM (
  input  [15:0] in_1,
  output [31:0] out_2
);

  // ROM #(.addrWidth(16), .line("quad")) rom_1: pin names not known; wires that end beside it: in_1, out_2[31:24], out_2[23:16], out_2[15:8], out_2[7:0]

  // Notes on the sheet:
  //   contents of rom_1 (hex, n*v repeats v):
  //   20 1 0 1 ac 1 0 1 8c 2 0 1 8c 43 0 0 8c 64
endmodule

module IF_ID (
  input  in_1,
  input  [31:0] in_2,
  input  [15:0] in_3,
  input  in_4,
  output [31:0] out_5,
  output [15:0] out_6
);

  Register #(.width(32)) register_1 (.D(in_2), .en(in_1), .clk(in_4), .Q(out_5));  // open: clr
  Register #(.width(16)) register_2 (.D(in_3), .en(in_1), .clk(in_4), .Q(out_6));  // open: clr

  // Notes on the sheet:
  //   INSTRUCTION
  //   NEW PC
  //   IF_ID WRITE
  //   CLK
endmodule

module IntructionFormater (
  input  [31:0] in_1,
  output [5:0] out_2,
  output [4:0] out_3,
  output [4:0] out_4,
  output [15:0] out_5,
  output [4:0] out_6,
  output [4:0] out_7,
  output [5:0] out_8
);


  assign out_2 = in_1[5:0];
  assign out_3 = in_1[10:6];
  assign out_4 = in_1[15:11];
  assign out_5 = in_1[15:0];
  assign out_6 = in_1[20:16];
  assign out_7 = in_1[25:21];
  assign out_8 = in_1[31:26];

  // Notes on the sheet:
  //   Instuction
  //   Func
  //   Shamt
  //   RD
  //   Immediate
  //   RT
  //   RS
  //   Opcode
endmodule

module ControlUnit (
  input  [5:0] OPcode,
  input  [5:0] Funct,
  output MemRead,
  output MemWrite,
  output MemToReg,
  output RegWrite,
  output RegDst,
  output Branch,
  output ALUsrc,
  output [3:0] out_10,
  output BNE
);

  wire nor_1_out;
  wire [11:0] rom_1_data, rom_2_data;

  ROM #(.addrWidth(6), .dataWidth(12)) rom_1 (.addr(OPcode), .data(rom_1_data));
  ROM #(.addrWidth(6), .dataWidth(12)) rom_2 (.addr(Funct), .data(rom_2_data));
  nor nor_1 (nor_1_out, OPcode[0], OPcode[1], OPcode[2], OPcode[3], OPcode[4], OPcode[5]);
  Multiplexer #(.width(12)) multiplexer_1 (
    .in0(rom_1_data), .in1(rom_2_data),
    .out({BNE, out_10, ALUsrc, Branch, RegDst, RegWrite, MemToReg, MemWrite, MemRead}), .sel(nor_1_out));

  // Notes on the sheet:
  //   contents of rom_1 (hex, n*v repeats v):
  //   4*0 420 c00 0 0 58 58 258 0 d8 1d8 4d8 20*0 5d 7*0 42
  //   contents of rom_2 (hex, n*v repeats v):
  //   288 0 308 388 28*0 8 8 408 0 88 188 488 108 0 0 208
  //   ALUop
endmodule

module ID_EX (
  input  in_1,
  input  in_2,
  input  in_3,
  input  RegWrite,
  input  RegDst,
  input  Branch,
  input  ALUsrc,
  input  [3:0] in_8,
  input  [4:0] in_9,
  input  BNE,
  input  [31:0] in_11,
  input  [31:0] in_12,
  input  [15:0] in_13,
  input  [15:0] in_14,
  input  [4:0] in_15,
  input  [4:0] in_16,
  input  [4:0] in_17,
  input  CLK,
  output out_19,
  output out_20,
  output out_21,
  output out_22,
  output out_23,
  output out_24,
  output out_25,
  output [3:0] out_26,
  output [4:0] out_27,
  output out_28,
  output [31:0] out_29,
  output [31:0] out_30,
  output [15:0] out_31,
  output [15:0] out_32,
  output [4:0] out_33,
  output [4:0] out_34,
  output [4:0] out_35
);

  Register #(.width(17)) register_1 (
    .D({BNE, in_9, in_8, ALUsrc, Branch, RegDst, RegWrite, in_3, in_2, in_1}), .en(1'b1), .clk(CLK),
    .Q({out_28, out_27, out_26, out_25, out_24, out_23, out_22, out_21, out_20, out_19}));  // open: clr
  Register #(.width(32)) register_2 (.D(in_11), .en(1'b1), .clk(CLK), .Q(out_29));  // open: clr
  Register #(.width(32)) register_3 (.D(in_12), .en(1'b1), .clk(CLK), .Q(out_30));  // open: clr
  Register #(.width(16)) register_4 (.D(in_13), .en(1'b1), .clk(CLK), .Q(out_31));  // open: clr
  Register #(.width(16)) register_5 (.D(in_14), .en(1'b1), .clk(CLK), .Q(out_32));  // open: clr
  Register #(.width(5)) register_6 (.D(in_15), .en(1'b1), .clk(CLK), .Q(out_33));  // open: clr
  Register #(.width(5)) register_7 (.D(in_16), .en(1'b1), .clk(CLK), .Q(out_34));  // open: clr
  Register #(.width(5)) register_8 (.D(in_17), .en(1'b1), .clk(CLK), .Q(out_35));  // open: clr

  // Notes on the sheet:
  //   MemRead
  //   MemWrite
  //   MemToReg
  //   ALUop
  //   Shamt
  //   A
  //   B
  //   Immediate
  //   NewPC
  //   RS
  //   RT
  //   RD
endmodule

module EX_MEM (
  input  in_1,
  input  in_2,
  input  in_3,
  input  in_4,
  input  Branch,
  input  BNE,
  input  Zero,
  input  [31:0] in_8,
  input  [15:0] in_9,
  input  [31:0] in_10,
  input  [4:0] in_11,
  input  CLK,
  output out_13,
  output out_14,
  output out_15,
  output out_16,
  output out_17,
  output out_18,
  output out_19,
  output [31:0] out_20,
  output [15:0] out_21,
  output [31:0] out_22,
  output [4:0] out_23
);

  Register #(.width(1)) register_1 (.D(in_1), .en(1'b1), .clk(CLK), .Q(out_13));  // open: clr
  Register #(.width(1)) register_2 (.D(in_2), .en(1'b1), .clk(CLK), .Q(out_14));  // open: clr
  Register #(.width(1)) register_3 (.D(in_3), .en(1'b1), .clk(CLK), .Q(out_15));  // open: clr
  Register #(.width(1)) register_4 (.D(in_4), .en(1'b1), .clk(CLK), .Q(out_16));  // open: clr
  Register #(.width(1)) register_5 (.D(Branch), .en(1'b1), .clk(CLK), .Q(out_17));  // open: clr
  Register #(.width(1)) register_6 (.D(BNE), .en(1'b1), .clk(CLK), .Q(out_18));  // open: clr
  Register #(.width(1)) register_7 (.D(Zero), .en(1'b1), .clk(CLK), .Q(out_19));  // open: clr
  Register #(.width(32)) register_8 (.D(in_8), .en(1'b1), .clk(CLK), .Q(out_20));  // open: clr
  Register #(.width(16)) register_9 (.D(in_9), .en(1'b1), .clk(CLK), .Q(out_21));  // open: clr
  Register #(.width(32)) register_10 (.D(in_10), .en(1'b1), .clk(CLK), .Q(out_22));  // open: clr
  Register #(.width(5)) register_11 (.D(in_11), .en(1'b1), .clk(CLK), .Q(out_23));  // open: clr

  // Notes on the sheet:
  //   MemWrite
  //   MemToReg
  //   ALUout
  //   BeqAddress
  //   WriteData
  //   RD
  //   MemRead
  //   RegWrite
endmodule

module DM (
  input  [31:0] in_1,
  input  in_2,
  input  in_3,
  input  CLK,
  input  [31:0] in_5,
  output [31:0] out_6
);

  wire not_1_out;

  not not_1 (not_1_out, CLK);
  RAM #(.addrWidth(16), .dataWidth(32)) ram_1 (
    .addr(in_1[15:0]), .we(in_2), .oe(in_3), .clk(not_1_out), .din(in_5), .dout(out_6));

  // Notes on the sheet:
  //   Address
  //   MemWrite
  //   MemRead
  //   Data
endmodule

module MEM_WB (
  input  in_1,
  input  in_2,
  input  [31:0] in_3,
  input  [31:0] in_4,
  input  [4:0] in_5,
  input  CLK,
  output out_7,
  output out_8,
  output [31:0] out_9,
  output [31:0] out_10,
  output [4:0] out_11
);

  Register #(.width(1)) register_1 (.D(in_1), .en(1'b1), .clk(CLK), .Q(out_7));  // open: clr
  Register #(.width(1)) register_2 (.D(in_2), .en(1'b1), .clk(CLK), .Q(out_8));  // open: clr
  Register #(.width(32)) register_3 (.D(in_3), .en(1'b1), .clk(CLK), .Q(out_9));  // open: clr
  Register #(.width(32)) register_4 (.D(in_4), .en(1'b1), .clk(CLK), .Q(out_10));  // open: clr
  Register #(.width(5)) register_5 (.D(in_5), .en(1'b1), .clk(CLK), .Q(out_11));  // open: clr

  // Notes on the sheet:
  //   MemToReg
  //   RegWrite
  //   ReadData
  //   ALUout
  //   RD
endmodule

module HazardUnit (
  input  [4:0] in_1,
  input  MemRead,
  input  [31:0] in_3,
  output IF_IDwrite,
  output Flush,
  output PCwrite
);

  wire and_1_out, comparator_1_eq, comparator_2_eq, nor_1_out, or_1_out;

  Comparator #(.width(5)) comparator_1 (.a(in_1), .b(in_3[20:16]), .eq(comparator_1_eq));  // open: gt, lt
  Comparator #(.width(5)) comparator_2 (.a(in_1), .b(in_3[25:21]), .eq(comparator_2_eq));  // open: gt, lt
  nor nor_1 (nor_1_out, in_1[0], in_1[1], in_1[2], in_1[3], in_1[4]);
  or or_1 (or_1_out, comparator_1_eq, comparator_2_eq);
  and and_1 (and_1_out, MemRead, or_1_out);
  Multiplexer multiplexer_1 (.in0(and_1_out), .in1(1'b0), .out(Flush), .sel(nor_1_out));
  not not_1 (IF_IDwrite, Flush);
  not not_2 (PCwrite, Flush);

  // Notes on the sheet:
  //   Instruction
  //   RD
endmodule

module ForwardingUnit (
  input  MemRW,
  input  [4:0] in_2,
  input  [4:0] in_3,
  input  [4:0] in_4,
  input  [4:0] in_5,
  input  WBRW,
  output [1:0] out_7,
  output [1:0] ForwrdB
);

  wire comparator_1_eq, comparator_2_eq, comparator_3_eq, comparator_4_eq;

  Comparator #(.width(5)) comparator_1 (.a(in_2), .b(in_3), .eq(comparator_1_eq));  // open: gt, lt
  Comparator #(.width(5)) comparator_2 (.a(in_2), .b(in_4), .eq(comparator_2_eq));  // open: gt, lt
  Comparator #(.width(5)) comparator_3 (.a(in_5), .b(in_3), .eq(comparator_3_eq));  // open: gt, lt
  Comparator #(.width(5)) comparator_4 (.a(in_5), .b(in_4), .eq(comparator_4_eq));  // open: gt, lt
  and and_1 (out_7[0], MemRW, comparator_1_eq);
  and and_2 (out_7[1], comparator_2_eq, WBRW);
  and and_3 (ForwrdB[0], comparator_3_eq, MemRW);
  and and_4 (ForwrdB[1], comparator_4_eq, WBRW);

  // Notes on the sheet:
  //   RS
  //   MemRD
  //   WBRD
  //   RT
  //   ForwardA
endmodule

module JumpControl (
  input  [31:0] in_1,
  output [15:0] out_2,
  output Jump
);

  wire and_1_out, and_2_out;

  and and_1 (and_1_out, in_1[26], in_1[27], ~in_1[28], ~in_1[29], ~in_1[30], ~in_1[31]);  // AND_Gate
  and and_2 (and_2_out, ~in_1[26], in_1[27], ~in_1[28], ~in_1[29], ~in_1[30], ~in_1[31]);  // AND_Gate
  or or_1 (Jump, and_1_out, and_2_out);

  assign out_2 = in_1[15:0];

  // Notes on the sheet:
  //   Instruction
  //   JumpAddress16bit
endmodule
